# Fritzing sketch FINAL PROJECT ARDUINO (saved by Fritzing 0.9.3b)
breadboards: 1

parts:
  부품1 = Arduino Uno (Rev3)  # not connected
  J1 = Piezo Speaker
  MIC1 = Microphone  # not connected
  S1 = Pushbutton [package="[THT]"]
  S2 = Pushbutton [package="[THT]"]
  R1 = Resistor [tolerance=±5% resistance=10k package=THT]  # not connected
  LED1 = LED - 5mm [color="Red (633nm)" package="5 mm [THT]"]  # not connected
  R4 = Resistor [tolerance=±5% resistance=10k package=THT]  # not connected
  R5 = Resistor [tolerance=±5% resistance=10k package=THT]  # not connected
  R3 = Resistor [tolerance=±5% resistance=220 package=THT]  # not connected

nets:
  N1: J1.pin1, S2.Pin_1, S2.Pin_2
  N2: S1.Pin_1, S1.Pin_2
  N3: S1.Pin_3, S1.Pin_4
